// Digital circuit circuito-F.dig as structural Verilog
module circuito_F (
  input  A,
  input  B,
  input  C,
  input  D,
  output E
);

  wire and_1_out, nand_1_out, nor_1_out, not_1_out, not_2_out, xor_1_out;

  not not_1 (not_1_out, A);
  not not_2 (not_2_out, D);
  xor xor_1 (xor_1_out, A, B, C);
  nor nor_1 (nor_1_out, B, D);
  nand nand_1 (nand_1_out, not_1_out, B, C, not_2_out);
  and and_1 (and_1_out, xor_1_out, nor_1_out);
  or or_1 (E, and_1_out, nand_1_out);
endmodule
