// Digital circuit somador-completo.dig as structural Verilog
module somador_completo (
  input  A,
  input  B,
  input  B_2,
  output D,
  output E
);

  wire and_1_out, and_2_out, or_2_out;

  or or_1 (E, and_1_out, and_2_out);
  and and_1 (and_1_out, or_2_out, B_2);
  and and_2 (and_2_out, B, A);
  or or_2 (or_2_out, B, A);
  xor xor_1 (D, B_2, B, A);
endmodule
