// Digital circuit and.dig as structural Verilog
module \and  (
  input  A,
  input  B
);

  wire nand_1_out, nand_2_out;

  nand nand_1 (nand_1_out, A, B);
  nand nand_2 (nand_2_out, nand_1_out, nand_1_out);
  LED led_1 (.in(nand_2_out));
endmodule
