// Digital circuit not.dig as structural Verilog
module \not  (
  input  NOT
);

  wire nand_1_out;

  nand nand_1 (nand_1_out, NOT, NOT);
  LED led_1 (.in(nand_1_out));

  // Notes on the sheet:
  //   NOT: Porta de negação
endmodule
